# Fritzing sketch schematic (saved by Fritzing 0.9.4)

parts:
  Pro_Micro3 = SparkFun Pro Micro
  S19 = Round Pushbutton
  S20 = Round Pushbutton
  S21 = Round Pushbutton
  S22 = Round Pushbutton
  S23 = Round Pushbutton
  S24 = Round Pushbutton  # not connected
  OLED3 = 128x32 I2C Monochrome OLED Display
  U3 = ENCODER_RGB_CA [package=encoder_led_3]

nets:
  GND: Pro_Micro3.GND, Pro_Micro3.RAW, OLED3.RST, OLED3.GND, U3.SW
  N1: Pro_Micro3.2, OLED3.SDA
  N2: Pro_Micro3.3, Pro_Micro3.4, OLED3.SCL
  N3: Pro_Micro3.5, S21.leg0
  N4: Pro_Micro3.6, S19.leg0
  N5: Pro_Micro3.7, S22.leg0
  N6: Pro_Micro3.8, S23.leg0
  N7: Pro_Micro3.9, S20.leg0
  N8: Pro_Micro3.A1, U3.-R
  N9: Pro_Micro3.A2, U3.-G
  VCC: Pro_Micro3.VCC, OLED3.VIN

custom parts:
  SparkFun Pro Micro: The Pro Micro is similar to the Pro Mini except with an ATmega32U4 on board. The USB transceiver inside the 32U4 allows us to add USB connectivity on-board and do away with bulky external USB interface. Based on: https://github.com/unorthodox-engineers/unorthodox-arduino/blob/master/Unorthodox/fritzing/parts/Pro%20Micro.fzpz
